# Fritzing sketch Edspert_Modul_8_1_Sensor (saved by Fritzing 0.9.3b)
breadboards: 1

parts:
  U1 = ESP32S-HiLetgo [part_number=ESP32S-HiLetgo]
  RHT2 = Humidity and Temperature Sensor RHT03 [part_number=DHT22]
  Mod1 = KY-018 Photoresistor Module [package="Breakout board"]
  Part1 = Soil Moisture Sensor

nets:
  VCC: U1.3.3, RHT2.Vcc, Mod1.Vin, Part1.VCC
  N1: U1.GPIO36, Mod1.S
  N2: U1.GPIO39, Part1.SIG
  N3: U1.GPIO14, RHT2.Data-signal
  GND: U1.GND, RHT2.GND_2, Mod1.-, Part1.GND

custom parts:
  ESP32S-HiLetgo: HiLetgo ESP-WROOM-32 ESP32 ESP-32S Development Board 2.4GHz Dual-Mode WiFi + Bluetooth Dual Cores Microcontroller The ESP32 integrated with Antenna switches, RF Balun, power amplifiers, low-noise amplifiers, filters, and management modules, and the entire solution occupies the least area of PCB. 2.4 GHz Wi-Fi plus Bluetooth dual-mode chip, with TSMC Ultra-low power consumption 40nm technology,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
  KY-018 Photoresistor Module: KY-018 Photoresistor module, used to measure light intensity. It can determine the presence or absence of light.
